// Logisim project simple-ff.circ as structural Verilog: 1 circuit, main circuit main
module main (
  input  CLK,
  output Q1,
  output Q2
);

  wire FF1_qn, FF2_qn, XOR1_out;

  J_K_Flip_Flop FF1 (.J(Q2), .K(FF2_qn), .clk(CLK), .Q(Q1), .Qn(FF1_qn));  // open: preset, reset
  D_Flip_Flop FF2 (.D(XOR1_out), .clk(CLK), .Q(Q2), .Qn(FF2_qn));  // open: preset, reset
  xor XOR1 (XOR1_out, Q2, FF1_qn);
endmodule
